# Fritzing sketch blackbox (saved by Fritzing 0.6.3b)
breadboards: 1

parts:
  Blue_SMiRF_Silver1 = BlueSMiRF Silver
  U1 = 3-Axis Accelerometer Breakout
  Arduino1 = Arduino
  Part1 = Sonar_MAXBotix_EZ
  Part2 = Arduino GPS Shield  # not connected

nets:
  N1: Blue_SMiRF_Silver1.connector0, Blue_SMiRF_Silver1.connector5
  N2: Blue_SMiRF_Silver1.connector1, Arduino1.D1TX
  N3: Blue_SMiRF_Silver1.connector2, Arduino1.D0RX
  GND: Blue_SMiRF_Silver1.connector3, U1.GND, Arduino1.GND, Part1.connector6
  VDD: Blue_SMiRF_Silver1.connector4, U1.VDD, Arduino1.+5V, Part1.connector1
  N4: U1.Z, Arduino1.D4
  N5: U1.Y, Arduino1.D3
  N6: U1.X, Arduino1.D2
  N7: Arduino1.A0, Part1.connector5
